// Logisim project Questao-1.circ as structural Verilog: 1 circuit, main circuit main
module main (
  input  CLR,
  output Q0,
  output Q1,
  output Q2
);

  wire and_1_out, clock_1_out;

  Clock clock_1 (.out(clock_1_out));
  T_Flip_Flop t_ff_1 (.clk(clock_1_out), .T(1'b1), .Q(Q0), .reset(CLR));  // open: Qn, preset, en
  T_Flip_Flop t_ff_2 (.clk(clock_1_out), .T(Q0), .Q(Q1), .reset(CLR));  // open: Qn, preset, en
  and and_1 (and_1_out, Q0, Q1);
  T_Flip_Flop t_ff_3 (.clk(clock_1_out), .T(and_1_out), .Q(Q2), .reset(CLR));  // open: Qn, preset, en

  // Notes on the sheet:
  //   1
  //   CLK
endmodule
