// Logisim project Questao-4A.circ as structural Verilog: 1 circuit, main circuit main
module main (
  input  CLK,
  output Q0,
  output Q1,
  output Q2,
  output Q3
);

  wire clock_1_out;

  Clock clock_1 (.out(clock_1_out));
  D_Flip_Flop d_ff_1 (.clk(clock_1_out), .D(CLK), .Q(Q0));  // open: Qn, preset, en, reset
  D_Flip_Flop d_ff_2 (.clk(clock_1_out), .D(Q0), .Q(Q1));  // open: Qn, preset, en, reset
  D_Flip_Flop d_ff_3 (.clk(clock_1_out), .D(Q1), .Q(Q2));  // open: Qn, preset, en, reset
  D_Flip_Flop d_ff_4 (.clk(clock_1_out), .D(Q2), .Q(Q3));  // open: Qn, preset, en, reset

  // Notes on the sheet:
  //   Entrada
endmodule
