// Logisim project Questao-3.circ as structural Verilog: 1 circuit, main circuit main
module main (
  input  UP_DOWN,
  input  CLR,
  output Q0,
  output Q1,
  output Q2
);

  wire and_1_out, clock_1_out, t_ff_1_q, t_ff_1_qn, t_ff_2_q, t_ff_2_qn, t_ff_3_qn;

  Clock clock_1 (.out(clock_1_out));
  xor xor_1 (Q0, UP_DOWN, t_ff_1_qn);
  T_Flip_Flop t_ff_1 (.clk(clock_1_out), .T(1'b1), .Q(t_ff_1_q), .Qn(t_ff_1_qn), .reset(CLR));  // open: preset, en
  xor xor_2 (Q1, UP_DOWN, t_ff_2_qn);
  T_Flip_Flop t_ff_2 (.clk(clock_1_out), .T(t_ff_1_q), .Q(t_ff_2_q), .Qn(t_ff_2_qn), .reset(CLR));  // open: preset, en
  and and_1 (and_1_out, t_ff_1_q, t_ff_2_q);
  xor xor_3 (Q2, UP_DOWN, t_ff_3_qn);
  T_Flip_Flop t_ff_3 (.clk(clock_1_out), .T(and_1_out), .Qn(t_ff_3_qn), .reset(CLR));  // open: Q, preset, en

  // Notes on the sheet:
  //   1
  //   CLK
endmodule
