// Logisim project Questao-4B.circ as structural Verilog: 1 circuit, main circuit main
module main (
  input  Q0,
  input  Q1,
  input  Q2,
  input  Q3,
  input  SHIFT_LOAD,
  output S0
);

  wire and_1_out, and_2_out, and_3_out, and_4_out, and_5_out, and_6_out, and_7_out, clock_1_out, d_ff_1_q,
       d_ff_2_q, d_ff_3_q, not_1_out, or_1_out, or_2_out, or_3_out;

  not not_1 (not_1_out, SHIFT_LOAD);
  Clock clock_1 (.out(clock_1_out));
  and and_1 (and_1_out, Q0, SHIFT_LOAD);
  and and_2 (and_2_out, d_ff_1_q, not_1_out);
  D_Flip_Flop d_ff_1 (.clk(clock_1_out), .D(and_1_out), .Q(d_ff_1_q));  // open: Qn, preset, en, reset
  and and_3 (and_3_out, Q1, SHIFT_LOAD);
  or or_1 (or_1_out, and_2_out, and_3_out);
  D_Flip_Flop d_ff_2 (.clk(clock_1_out), .D(or_1_out), .Q(d_ff_2_q));  // open: Qn, preset, en, reset
  and and_4 (and_4_out, d_ff_2_q, not_1_out);
  and and_5 (and_5_out, Q2, SHIFT_LOAD);
  or or_2 (or_2_out, and_4_out, and_5_out);
  D_Flip_Flop d_ff_3 (.clk(clock_1_out), .D(or_2_out), .Q(d_ff_3_q));  // open: Qn, preset, en, reset
  and and_6 (and_6_out, d_ff_3_q, not_1_out);
  or or_3 (or_3_out, and_6_out, and_7_out);
  and and_7 (and_7_out, Q3, SHIFT_LOAD);
  D_Flip_Flop d_ff_4 (.clk(clock_1_out), .D(or_3_out), .Q(S0));  // open: Qn, preset, en, reset

  // Notes on the sheet:
  //   CLR
endmodule
