// Logisim project Questao-8.circ as structural Verilog: 1 circuit, main circuit main
module main (
  input  S0,
  input  CLR,
  input  S1,
  input  S2,
  input  S3,
  input  EJ,
  input  EA,
  input  EB,
  input  CLR_2,
  input  CLR_3,
  input  CLR_4,
  output Q0,
  output Q1,
  output Q2,
  output Q3
);

  wire adder_1_cout, adder_1_out, adder_2_cout, adder_2_out, adder_3_cout, adder_3_out, adder_4_out,
       clock_1_out, d_ff_1_q, d_ff_2_q, d_ff_3_q, d_ff_4_q, d_ff_5_q, d_ff_6_q, d_ff_7_q, d_ff_8_q, d_ff_9_q,
       d_ff_10_q, d_ff_11_q, d_ff_12_q;

  Clock clock_1 (.out(clock_1_out));
  D_Flip_Flop d_ff_1 (.clk(clock_1_out), .D(S0), .Q(d_ff_1_q), .en(EJ), .reset(CLR_3));  // open: Qn, preset
  D_Flip_Flop d_ff_2 (.clk(clock_1_out), .D(S1), .Q(d_ff_2_q), .en(EJ), .reset(CLR_3));  // open: Qn, preset
  D_Flip_Flop d_ff_3 (.clk(clock_1_out), .D(S2), .Q(d_ff_3_q), .en(EJ), .reset(CLR_3));  // open: Qn, preset
  D_Flip_Flop d_ff_4 (.clk(clock_1_out), .D(S3), .Q(d_ff_4_q), .en(EJ), .reset(CLR_3));  // open: Qn, preset
  D_Flip_Flop d_ff_5 (.clk(clock_1_out), .D(d_ff_1_q), .Q(d_ff_5_q), .en(EB), .reset(CLR_4));  // open: Qn, preset
  D_Flip_Flop d_ff_6 (.clk(clock_1_out), .D(d_ff_1_q), .Q(d_ff_6_q), .en(EA), .reset(CLR));  // open: Qn, preset
  Adder #(.width(1)) adder_1 (.a(d_ff_6_q), .b(d_ff_5_q), .out(adder_1_out), .cout(adder_1_cout));  // open: cin
  D_Flip_Flop d_ff_7 (.clk(clock_1_out), .D(d_ff_2_q), .Q(d_ff_7_q), .en(EA), .reset(CLR));  // open: Qn, preset
  Adder #(.width(1)) adder_2 (.a(d_ff_7_q), .b(d_ff_8_q), .out(adder_2_out), .cin(adder_1_cout), .cout(adder_2_cout));
  D_Flip_Flop d_ff_8 (.clk(clock_1_out), .D(d_ff_2_q), .Q(d_ff_8_q), .en(EB), .reset(CLR_4));  // open: Qn, preset
  D_Flip_Flop d_ff_9 (.clk(clock_1_out), .D(d_ff_3_q), .Q(d_ff_9_q), .en(EA), .reset(CLR));  // open: Qn, preset
  Adder #(.width(1)) adder_3 (.a(d_ff_9_q), .b(d_ff_10_q), .out(adder_3_out), .cin(adder_2_cout), .cout(adder_3_cout));
  D_Flip_Flop d_ff_10 (.clk(clock_1_out), .D(d_ff_3_q), .Q(d_ff_10_q), .en(EB), .reset(CLR_4));  // open: Qn, preset
  D_Flip_Flop d_ff_11 (.clk(clock_1_out), .D(d_ff_4_q), .Q(d_ff_11_q), .en(EA), .reset(CLR));  // open: Qn, preset
  Adder #(.width(1)) adder_4 (.a(d_ff_11_q), .b(d_ff_12_q), .out(adder_4_out), .cin(adder_3_cout));  // open: cout
  D_Flip_Flop d_ff_12 (.clk(clock_1_out), .D(d_ff_4_q), .Q(d_ff_12_q), .en(EB), .reset(CLR_4));  // open: Qn, preset
  D_Flip_Flop d_ff_13 (.clk(clock_1_out), .D(adder_1_out), .Q(Q0), .reset(CLR_2));  // open: Qn, preset, en
  D_Flip_Flop d_ff_14 (.clk(clock_1_out), .D(adder_2_out), .Q(Q1), .reset(CLR_2));  // open: Qn, preset, en
  D_Flip_Flop d_ff_15 (.clk(clock_1_out), .D(adder_3_out), .Q(Q2), .reset(CLR_2));  // open: Qn, preset, en
  D_Flip_Flop d_ff_16 (.clk(clock_1_out), .D(adder_4_out), .Q(Q3), .reset(CLR_2));  // open: Qn, preset, en

  // Notes on the sheet:
  //   CLK
endmodule
