// Logisim project Questao-9.circ as structural Verilog: 2 circuits, main circuit main
module FSM1 (
  input  S0,
  input  S1,
  input  S2,
  input  S3,
  input  INICIO,
  output Q0,
  output Q1,
  output Q2,
  output Q3
);

  wire adder_1_cout, adder_1_out, adder_2_cout, adder_2_out, adder_3_cout, adder_3_out, adder_4_out,
       and_1_out, CLK_out, d_ff_1_q, d_ff_2_q, d_ff_3_q, d_ff_4_q, d_ff_5_q, d_ff_6_q, d_ff_7_q, d_ff_8_q,
       d_ff_9_q, d_ff_10_q, d_ff_11_q, d_ff_12_q, main_1_clr, main_1_ea, main_1_eb, main_1_ei, main_1_eo,
       main_1_halt, not_1_out;

  and and_1 (and_1_out, CLK_out, not_1_out);
  Clock CLK (.out(CLK_out));
  not not_1 (not_1_out, main_1_halt);
  main main_1 (
    .CLK(CLK_out), .EI(main_1_ei), .EB(main_1_eb), .EA(main_1_ea), .HALT(main_1_halt), .EO(main_1_eo),
    .INICIO(INICIO), .CLR(main_1_clr));
  D_Flip_Flop d_ff_1 (.clk(and_1_out), .D(S0), .Q(d_ff_1_q), .en(main_1_ei), .reset(main_1_clr));  // open: Qn, preset
  D_Flip_Flop d_ff_2 (.clk(and_1_out), .D(S1), .Q(d_ff_2_q), .en(main_1_ei), .reset(main_1_clr));  // open: Qn, preset
  D_Flip_Flop d_ff_3 (.clk(and_1_out), .D(S2), .Q(d_ff_3_q), .en(main_1_ei), .reset(main_1_clr));  // open: Qn, preset
  D_Flip_Flop d_ff_4 (.clk(and_1_out), .D(S3), .Q(d_ff_4_q), .en(main_1_ei), .reset(main_1_clr));  // open: Qn, preset
  D_Flip_Flop d_ff_5 (
    .clk(and_1_out), .D(d_ff_1_q), .Q(d_ff_5_q), .en(main_1_eb), .reset(main_1_clr));  // open: Qn, preset
  D_Flip_Flop d_ff_6 (
    .clk(and_1_out), .D(d_ff_1_q), .Q(d_ff_6_q), .en(main_1_ea), .reset(main_1_clr));  // open: Qn, preset
  Adder #(.width(1)) adder_1 (.a(d_ff_6_q), .b(d_ff_5_q), .out(adder_1_out), .cout(adder_1_cout));  // open: cin
  D_Flip_Flop d_ff_7 (
    .clk(and_1_out), .D(d_ff_2_q), .Q(d_ff_7_q), .en(main_1_ea), .reset(main_1_clr));  // open: Qn, preset
  Adder #(.width(1)) adder_2 (.a(d_ff_7_q), .b(d_ff_8_q), .out(adder_2_out), .cin(adder_1_cout), .cout(adder_2_cout));
  D_Flip_Flop d_ff_8 (
    .clk(and_1_out), .D(d_ff_2_q), .Q(d_ff_8_q), .en(main_1_eb), .reset(main_1_clr));  // open: Qn, preset
  D_Flip_Flop d_ff_9 (
    .clk(and_1_out), .D(d_ff_3_q), .Q(d_ff_9_q), .en(main_1_ea), .reset(main_1_clr));  // open: Qn, preset
  Adder #(.width(1)) adder_3 (.a(d_ff_9_q), .b(d_ff_10_q), .out(adder_3_out), .cin(adder_2_cout), .cout(adder_3_cout));
  D_Flip_Flop d_ff_10 (
    .clk(and_1_out), .D(d_ff_3_q), .Q(d_ff_10_q), .en(main_1_eb), .reset(main_1_clr));  // open: Qn, preset
  D_Flip_Flop d_ff_11 (
    .clk(and_1_out), .D(d_ff_4_q), .Q(d_ff_11_q), .en(main_1_ea), .reset(main_1_clr));  // open: Qn, preset
  Adder #(.width(1)) adder_4 (.a(d_ff_11_q), .b(d_ff_12_q), .out(adder_4_out), .cin(adder_3_cout));  // open: cout
  D_Flip_Flop d_ff_12 (
    .clk(and_1_out), .D(d_ff_4_q), .Q(d_ff_12_q), .en(main_1_eb), .reset(main_1_clr));  // open: Qn, preset
  D_Flip_Flop d_ff_13 (
    .clk(and_1_out), .D(adder_1_out), .Q(Q0), .preset(main_1_eo), .en(main_1_eo), .reset(main_1_clr));  // open: Qn
  D_Flip_Flop d_ff_14 (
    .clk(and_1_out), .D(adder_2_out), .Q(Q1), .en(main_1_eo), .reset(main_1_clr));  // open: Qn, preset
  D_Flip_Flop d_ff_15 (
    .clk(and_1_out), .D(adder_3_out), .Q(Q2), .preset(main_1_eo), .en(main_1_eo), .reset(main_1_clr));  // open: Qn
  D_Flip_Flop d_ff_16 (
    .clk(and_1_out), .D(adder_4_out), .Q(Q3), .en(main_1_eo), .reset(main_1_clr));  // open: Qn, preset
endmodule

module main (
  input  CLK,
  input  INICIO,
  output EI,
  output EA,
  output EB,
  output EO,
  output HALT,
  output CLR
);

  wire and_1_out, and_2_out, and_3_out, d_ff_1_q, d_ff_2_q, d_ff_3_q, not_1_out, not_2_out, not_3_out,
       not_4_out, not_5_out, not_6_out, not_7_out, not_8_out, not_9_out, or_1_out, or_2_out, or_3_out;

  and and_1 (and_1_out, d_ff_2_q, d_ff_3_q);
  and and_2 (and_2_out, d_ff_2_q, not_1_out);
  not not_1 (not_1_out, d_ff_3_q);
  not not_2 (not_2_out, d_ff_1_q);
  not not_3 (not_3_out, d_ff_2_q);
  and and_3 (and_3_out, not_2_out, not_3_out, d_ff_3_q);
  not not_4 (not_4_out, d_ff_3_q);
  or or_1 (or_1_out, d_ff_1_q, and_1_out);
  or or_2 (or_2_out, and_2_out, and_3_out);
  or or_3 (or_3_out, not_4_out, d_ff_1_q);
  D_Flip_Flop d_ff_1 (.clk(CLK), .D(or_1_out), .Q(d_ff_1_q), .reset(INICIO));  // open: Qn, preset, en
  D_Flip_Flop d_ff_2 (.clk(CLK), .D(or_2_out), .Q(d_ff_2_q), .reset(INICIO));  // open: Qn, preset, en
  D_Flip_Flop d_ff_3 (.clk(CLK), .D(or_3_out), .Q(d_ff_3_q), .reset(INICIO));  // open: Qn, preset, en
  not not_5 (not_5_out, d_ff_1_q);
  and and_4 (EI, not_5_out, not_6_out);
  not not_6 (not_6_out, d_ff_3_q);
  not not_7 (not_7_out, d_ff_1_q);
  not not_8 (not_8_out, d_ff_2_q);
  and and_5 (EA, not_7_out, not_8_out, d_ff_3_q);
  and and_6 (EB, d_ff_2_q, d_ff_3_q);
  and and_7 (EO, d_ff_1_q, not_9_out);
  not not_9 (not_9_out, d_ff_3_q);
  and and_8 (HALT, d_ff_1_q, d_ff_3_q);

  assign CLR = INICIO;
endmodule
