// Logisim project Questao-2.circ as structural Verilog: 1 circuit, main circuit main
module main (
  input  CLR,
  output Q0,
  output Q1,
  output Q2
);

  wire and_1_out, clock_1_out, t_ff_1_q, t_ff_2_q;

  Clock clock_1 (.out(clock_1_out));
  T_Flip_Flop t_ff_1 (.clk(clock_1_out), .T(1'b1), .Q(t_ff_1_q), .Qn(Q0), .reset(CLR));  // open: preset, en
  T_Flip_Flop t_ff_2 (.clk(clock_1_out), .T(t_ff_1_q), .Q(t_ff_2_q), .Qn(Q1), .reset(CLR));  // open: preset, en
  and and_1 (and_1_out, t_ff_1_q, t_ff_2_q);
  T_Flip_Flop t_ff_3 (.clk(clock_1_out), .T(and_1_out), .Qn(Q2), .reset(CLR));  // open: Q, preset, en

  // Notes on the sheet:
  //   1
  //   CLK
endmodule
